// Logisim project FINALVERSION.circ as structural Verilog: 7 circuits, main circuit fileRegister
module fileRegister (
  input  [2:0] rs1,
  input  [2:0] rd,
  input  [2:0] rs2,
  input  RegWrite,
  input  in_5,
  input  [15:0] BusW,
  output [15:0] R0,
  output [15:0] out_8,
  output [15:0] out_9,
  output [15:0] out_10,
  output [15:0] out_11,
  output [15:0] out_12,
  output [15:0] out_13,
  output [15:0] out_14,
  output [15:0] BusA,
  output [15:0] busB
);

  wire and_1_out, and_2_out, and_3_out, and_4_out, and_5_out, and_6_out, and_7_out, decoder_1_out0,
       decoder_1_out1, decoder_1_out2, decoder_1_out3, decoder_1_out4, decoder_1_out5, decoder_1_out6,
       decoder_1_out7;

  Decoder #(.select(3), .enable("false")) decoder_1 (
    .out0(decoder_1_out0), .out1(decoder_1_out1), .out2(decoder_1_out2), .out3(decoder_1_out3),
    .out4(decoder_1_out4), .out5(decoder_1_out5), .out6(decoder_1_out6), .out7(decoder_1_out7), .sel(rd));
  and and_1 (and_1_out, decoder_1_out1, RegWrite);
  and and_2 (and_2_out, decoder_1_out2, RegWrite);
  and and_3 (and_3_out, decoder_1_out3, RegWrite);
  and and_4 (and_4_out, decoder_1_out4, RegWrite);
  and and_5 (and_5_out, decoder_1_out5, RegWrite);
  and and_6 (and_6_out, decoder_1_out6, RegWrite);
  and and_7 (and_7_out, RegWrite, decoder_1_out7);
  Register #(.width(16)) R1 (.D(BusW), .en(and_1_out), .Q(out_8), .clk(in_5));  // open: clr
  Register #(.width(16)) R2 (.D(BusW), .en(and_2_out), .Q(out_11), .clk(in_5));  // open: clr
  Register #(.width(16)) R3 (.D(BusW), .en(and_3_out), .Q(out_13), .clk(in_5));  // open: clr
  Register #(.width(16)) R4 (.D(BusW), .en(and_4_out), .Q(out_9), .clk(in_5));  // open: clr
  Register #(.width(16)) R5 (.D(BusW), .en(and_5_out), .Q(out_10), .clk(in_5));  // open: clr
  Register #(.width(16)) R6 (.D(BusW), .en(and_6_out), .Q(out_12), .clk(in_5));  // open: clr
  Register #(.width(16)) R7 (.D(BusW), .en(and_7_out), .Q(out_14), .clk(in_5));  // open: clr
  Multiplexer #(.select(3), .width(16), .enable("false")) multiplexer_1 (
    .in0({16{1'b0}}), .in1(out_8), .in2(out_11), .in3(out_13), .in4(out_9), .in5(out_10), .in6(out_12),
    .in7(out_14), .out(BusA), .sel(rs1));
  Multiplexer #(.select(3), .width(16), .enable("false")) multiplexer_2 (
    .in0({16{1'b0}}), .in1(out_8), .in2(out_11), .in3(out_13), .in4(out_9), .in5(out_10), .in6(out_12),
    .in7(out_14), .out(busB), .sel(rs2));

  assign R0 = {16{1'b0}};

  // Other names for the same wires on the sheet: R1[15:0] = out_8; R2[15:0] = out_11; R3[15:0] = out_13;
  //   R4[15:0] = out_9; R5[15:0] = out_10; R6[15:0] = out_12; R7[15:0] = out_14

  // Notes on the sheet:
  //   THIS IS WRITING
  //   SHOW CASING OUTPUT
endmodule

module ALU (
  input  [15:0] in_1,
  input  [15:0] in_2,
  input  [3:0] in_3,
  output [15:0] result,
  output [2:0] out_5
);

  wire comparator_1_lt, comparator_2_lt;
  wire [15:0] adder_1_out, ANDOP, LUI, NOROP, ORAB, ROR, SLL, SLTAB, SLTUAB, SRA, SRL, subtractor_1_out,
       XOROP;

  assign SLTUAB = {{15{1'b0}}, comparator_1_lt};  // Bit_Extender bit_extender_1
  Comparator #(.width(16), .mode("unsigned")) comparator_1 (.a(in_1), .b(in_2), .lt(comparator_1_lt));  // open: gt, eq
  Comparator #(.width(16)) comparator_2 (.a(in_1), .b(in_2), .lt(comparator_2_lt));  // open: gt, eq
  Shifter #(.width(16)) shifter_1 (.in(in_1), .\dist (in_2[3:0]), .out(SLL));
  Shifter #(.width(16), .shift("lr")) shifter_2 (.in(in_1), .\dist (in_2[3:0]), .out(SRL));
  Shifter #(.width(16), .shift("ar")) shifter_3 (.in(in_1), .\dist (in_2[3:0]), .out(SRA));
  Shifter #(.width(16), .shift("rr")) shifter_4 (.in(in_1), .\dist (in_2[3:0]), .out(ROR));
  assign SLTAB = {{15{1'b0}}, comparator_2_lt};  // Bit_Extender bit_extender_2
  Subtractor #(.width(16)) subtractor_1 (.a(in_1), .b(in_2), .out(subtractor_1_out));  // open: bin, bout
  Shifter #(.width(16)) shifter_5 (.in(in_2), .\dist (4'b0101), .out(LUI));
  Adder #(.width(16)) adder_1 (.a(in_1), .b(in_2), .out(adder_1_out));  // open: cin, cout
  assign XOROP = in_1 ^ in_2;  // XOR_Gate XOR, 16 bits wide
  assign ANDOP = in_1 & in_2;  // AND_Gate AND, 16 bits wide
  assign NOROP = ~(in_1 | in_2);  // NOR_Gate NOR, 16 bits wide
  assign ORAB = in_1 | in_2;  // OR_Gate or_1, 16 bits wide
  Multiplexer #(.select(4), .width(16), .enable("false")) multiplexer_1 (
    .in0(adder_1_out), .in1(subtractor_1_out), .in2(SLTAB), .in3(SLTUAB), .in4(XOROP), .in5(ORAB),
    .in6(ANDOP), .in7(NOROP), .in8(SLL), .in9(SRL), .in10(SRA), .in11(ROR), .in12(LUI), .out(result),
    .sel(in_3));  // open: in13, in14, in15
  Comparator #(.width(16)) comparator_3 (.a(in_1), .b(in_2), .gt(out_5[0]), .eq(out_5[1]), .lt(out_5[2]));

  // Other names for the same wires on the sheet: A[15:0] = in_1; B[15:0] = in_2; B_0__5[3:0] = in_2[3:0]

  // Notes on the sheet:
  //   SLTU
  //   SLT
endmodule

module CNTRL (
  input  [4:0] opcode,
  input  [1:0] f,
  output [1:0] out_3,
  output out_4,
  output [1:0] out_5,
  output out_6,
  output out_7,
  output [1:0] out_8,
  output [3:0] aluop,
  output BEQ,
  output BNQ,
  output BLT,
  output BGE,
  output Jump
);

  wire comparator_1_gt, comparator_6_gt, comparator_7_eq;
  wire [3:0] rom_1_data;

  Comparator #(.width(5), .mode("unsigned")) comparator_1 (
    .a(opcode), .b(5'b00010), .gt(comparator_1_gt));  // open: eq, lt
  ROM #(.addrWidth(5), .dataWidth(4)) rom_1 (.addr(opcode), .data(rom_1_data));  // open: sel
  Multiplexer #(.width(4), .enable("false")) multiplexer_1 (
    .in0({opcode[1:0], f}), .in1(rom_1_data), .out(aluop), .sel(comparator_1_gt));
  ROM #(.addrWidth(5), .dataWidth(9)) rom_2 (
    .addr(opcode), .data({out_3, out_4, out_5, out_6, out_7, out_8}));  // open: sel
  Comparator #(.width(5), .mode("unsigned")) comparator_2 (.a(opcode), .b(5'b10010), .eq(BEQ));  // open: gt, lt
  Comparator #(.width(5), .mode("unsigned")) comparator_3 (.a(5'b10011), .b(opcode), .eq(BNQ));  // open: gt, lt
  Comparator #(.width(5), .mode("unsigned")) comparator_4 (.a(5'b10100), .b(opcode), .eq(BLT));  // open: gt, lt
  Comparator #(.width(5), .mode("unsigned")) comparator_5 (.a(5'b10101), .b(opcode), .eq(BGE));  // open: gt, lt
  or or_1 (Jump, comparator_6_gt, comparator_7_eq);
  Comparator #(.width(5), .mode("unsigned")) comparator_6 (
    .a(opcode), .b(5'b10111), .gt(comparator_6_gt));  // open: eq, lt
  Comparator #(.width(5), .mode("unsigned")) comparator_7 (
    .a(5'b10110), .b(opcode), .eq(comparator_7_eq));  // open: gt, lt

  // Other names for the same wires on the sheet: OP[4:0] = opcode

  // Notes on the sheet:
  //   contents of rom_1 (hex, n*v repeats v):
  //   6*0 2 3 4 5 6 7 8 9 a b 7*0 c
  //   contents of rom_2 (hex, n*v repeats v):
  //   40 40 40 0 d0 0 d0 d0 8*e0 e5 18 4*0 c2 170 0 1c2
  //   COMPARISION
endmodule

module main (
  output [15:0] out_1,
  output [15:0] out_2,
  output [15:0] out_3,
  output [15:0] out_4,
  output [15:0] out_5,
  output [15:0] out_6,
  output [15:0] out_7,
  output [15:0] out_8,
  output [15:0] out_9,
  output [1:0] out_10,
  output [1:0] out_11
);

  wire BEQ, BGE, BLT, BNE, clk, J, KILL1, KILL2, MemRd, MemRed, MemWrite, nstall, or_1_out, RegWrite, STALL,
       WrEx, WrMem;
  wire [1:0] ALUB, BusWR, cntrl_1_out_5, cntrl_1_out_8, EXC_q, EXC_q_3, f, PC_ctrl, RegDis;
  wire [2:0] comp, imm5, multiplexer_3_out, RD2, RD3, RD4;
  wire [3:0] ALUO, ALUOP, cntrl_1_beq;
  wire [4:0] op;
  wire [4:4] B_EX_q;
  wire [5:0] imm11;
  wire [7:7] EXC_q_2;
  wire [10:6] cntrl_1_out_7;
  wire [12:0] MEM_q, multiplexer_4_out;
  wire [15:0] A0, adder_3_out, ALURes, B0, BusA, BusA___imm5s, BusB, D_q, imm5s, imm5SR_q, imm5z, imm5zR_q,
       imm11S, imm11SR_q, multiplexer_1_out, multiplexer_2_out, multiplexer_5_out, multiplexer_6_out,
       multiplexer_7_out, PC, PC___1, PC___1i, PC___imm5s, PC___imm11s, PCJ, Prev1, Prev2, ram_1_data,
       rom_1_data;

  assign imm11S = {{5{f[1]}}, {f, imm5, imm11}};  // Bit_Extender bit_extender_1
  assign imm5z = {{11{1'b0}}, {f, imm5}};  // Bit_Extender bit_extender_2
  assign imm5s = {{11{f[1]}}, {f, imm5}};  // Bit_Extender bit_extender_3
  Adder #(.width(16)) adder_1 (.a(imm11S), .b(PCJ), .out(PC___imm11s));  // open: cin, cout
  Clock clock_1 (.out(clk));
  not not_1 (nstall, STALL);
  Multiplexer #(.select(2), .width(16), .enable("false")) multiplexer_1 (
    .in0(PC___1i), .in1(PC___imm11s), .in2(PC___imm5s), .in3(BusA___imm5s), .out(multiplexer_1_out),
    .sel(PC_ctrl));
  Adder #(.width(16)) adder_2 (.a(16'h1), .b(PC), .out(PC___1i));  // open: cin, cout
  Register #(.width(16)) u_PC (.D(multiplexer_1_out), .en(nstall), .Q(PC), .clk(clk));  // open: clr
  Register #(.width(16)) NPC (.D(PC___1i), .Q(PC___1), .clk(clk));  // open: en, clr
  Register #(.width(16)) register_1 (.D(adder_3_out), .Q(PC___imm5s), .clk(clk));  // open: en, clr
  Adder #(.width(16)) adder_3 (.a(imm5s), .b(PCJ), .out(adder_3_out));  // open: cin, cout
  Adder #(.width(16)) adder_4 (.a(imm5s), .b(BusA), .out(BusA___imm5s));  // open: cin, cout
  Subtractor #(.width(16)) subtractor_1 (.a(PC___1), .b(16'h1), .out(PCJ));  // open: bin, bout
  ROM #(.addrWidth(16), .dataWidth(16)) rom_1 (.addr(PC), .data(rom_1_data));  // open: sel
  Register #(.width(16)) INST (.D(multiplexer_2_out), .en(nstall), .Q({f, imm5, imm11, op}), .clk(clk));  // open: clr
  Multiplexer #(.width(16), .enable("false")) multiplexer_2 (
    .in0(rom_1_data), .in1({16{1'b0}}), .out(multiplexer_2_out), .sel(KILL1));
  CNTRL cntrl_1 (
    .opcode(op), .f(f), .aluop(ALUO), .out_3(RegDis), .out_4(cntrl_1_out_7[10]), .out_5(cntrl_1_out_5),
    .out_6(cntrl_1_out_7[7]), .out_7(cntrl_1_out_7[6]), .out_8(cntrl_1_out_8), .BEQ(cntrl_1_beq[0]),
    .BNQ(cntrl_1_beq[1]), .BLT(cntrl_1_beq[2]), .BGE(cntrl_1_beq[3]), .Jump(J));
  Register #(.width(5)) B_EX (.D({J, cntrl_1_beq}), .Q({B_EX_q[4], BGE, BLT, BNE, BEQ}), .clk(clk));  // open: en, clr
  Multiplexer #(.select(2), .width(3), .enable("false")) multiplexer_3 (
    .in0(imm5), .in1(imm11[5:3]), .in2(3'b001), .in3(3'b111), .out(multiplexer_3_out), .sel(RegDis));
  Register #(.width(3)) u_RD2 (.D(multiplexer_3_out), .Q(RD2), .clk(clk));  // open: en, clr
  Multiplexer #(.width(13), .enable("false")) multiplexer_4 (
    .in0({RegDis, cntrl_1_out_7[10], cntrl_1_out_5, cntrl_1_out_7[7:6], cntrl_1_out_8, ALUO}),
    .in1({13{1'b0}}), .out(multiplexer_4_out), .sel(or_1_out));
  or or_1 (or_1_out, KILL2, STALL);
  PC_ctrl pc_ctrl_1 (
    .in_1(comp), .in_2(op), .in_5(BNE), .in_6(BLT), .in_7(BGE), .in_4(BEQ), .in_3(J), .PCCNTRL(PC_ctrl),
    .KILL1(KILL1), .KILL2(KILL2));
  Register #(.width(3)) u_RD3 (.D(RD2), .Q(RD3), .clk(clk));  // open: en, clr
  Register #(.width(13)) MEM (
    .D({EXC_q_3, WrEx, ALUB, EXC_q_2[7], MemRd, EXC_q, ALUOP}),
    .Q({MEM_q[12:11], WrMem, MEM_q[9:8], MemWrite, MemRed, BusWR, MEM_q[3:0]}), .clk(clk));  // open: en, clr
  Register #(.width(13)) EXC (
    .D(multiplexer_4_out), .Q({EXC_q_3, WrEx, ALUB, EXC_q_2[7], MemRd, EXC_q, ALUOP}), .clk(clk));  // open: en, clr
  Register #(.width(3)) u_RD4 (.D(RD3), .Q(RD4), .clk(clk));  // open: en, clr
  fileRegister fileregister_1 (
    .rd(RD4), .RegWrite(RegWrite), .BusW(out_9), .rs1(imm11[2:0]), .rs2(imm11[5:3]), .BusA(A0), .busB(B0),
    .in_5(clk), .out_9(out_5), .out_10(out_6), .out_12(out_7), .out_8(out_2), .out_11(out_3), .out_13(out_4),
    .R0(out_1), .out_14(out_8));
  Register #(.width(1)) WB (.D(WrMem), .Q(RegWrite), .clk(clk));  // open: en, clr
  Multiplexer #(.select(2), .width(16), .enable("false")) multiplexer_5 (
    .in0(A0), .in1(Prev1), .in2(Prev2), .in3(out_9), .out(multiplexer_5_out), .sel(out_10));
  Multiplexer #(.select(2), .width(16), .enable("false")) multiplexer_6 (
    .in0(B0), .in1(Prev1), .in2(Prev2), .in3(out_9), .out(multiplexer_6_out), .sel(out_11));
  Register #(.width(16)) A (.D(multiplexer_5_out), .Q(BusA), .clk(clk));  // open: en, clr
  Register #(.width(16)) B (.D(multiplexer_6_out), .Q(BusB), .clk(clk));  // open: en, clr
  Register #(.width(16)) imm5SR (.D(imm5s), .Q(imm5SR_q), .clk(clk));  // open: en, clr
  Forward forward_1 (
    .RS(imm11[2:0]), .Rt(imm11[5:3]), .RD2(RD2), .RD3(RD3), .Rd4(RD4), .WrEx(WrEx), .WrMem(WrMem),
    .WrWb(RegWrite), .FrwA(out_10), .FrwB(out_11), .in_6(MemRd), .out_12(STALL));
  Register #(.width(16)) imm5zR (.D(imm5z), .Q(imm5zR_q), .clk(clk));  // open: en, clr
  Register #(.width(16)) imm11SR (.D(imm11S), .Q(imm11SR_q), .clk(clk));  // open: en, clr
  Multiplexer #(.select(2), .width(16), .enable("false")) multiplexer_7 (
    .in0(BusB), .in1(imm5SR_q), .in2(imm5zR_q), .in3(imm11SR_q), .out(multiplexer_7_out), .sel(ALUB));
  ALU alu_1 (.result(Prev1), .in_3(ALUOP), .in_1(BusA), .in_2(multiplexer_7_out), .out_5(comp));
  Register #(.width(16)) Result (.D(Prev1), .Q(ALURes), .clk(clk));  // open: en, clr
  Register #(.width(16)) D (.D(BusB), .Q(D_q), .clk(clk));  // open: en, clr
  RAM #(.addrWidth(16), .dataWidth(16), .bus("separate")) ram_1 (
    .addr(ALURes), .din(D_q), .data(ram_1_data), .str(MemWrite), .clk(clk), .ld(MemRed));  // open: sel, clr
  Multiplexer #(.select(2), .width(16), .enable("false")) multiplexer_8 (
    .in0(ALURes), .in1(ram_1_data), .in2(PC___1), .out(Prev2), .sel(BusWR));  // open: in3
  Register #(.width(16)) Data (.D(Prev2), .Q(out_9), .clk(clk));  // open: en, clr

  // Other names for the same wires on the sheet: rs[2:0] = imm11[2:0]; rt[2:0] = imm11[5:3]; imm11[10:6] = {f, imm5};
  //   rd[2:0] = imm5; imm5[4:3] = f; BusW[15:0] = out_9; FrwA[1:0] = out_10; FrwB[1:0] = out_11; R0[15:0] = out_1;
  //   R1[15:0] = out_2; R2[15:0] = out_3; R3[15:0] = out_4; R4[15:0] = out_5; R5[15:0] = out_6; R6[15:0] = out_7;
  //   R7[15:0] = out_8

  // Notes on the sheet:
  //   DISPLAYING FILE REGISTER
  //   contents of rom_1 (hex, n*v repeats v):
  //   39 3052 2813 2615 18d4 37 58 1104 18
  //   DECODE
  //   EXC
  //   MEM
endmodule

module PC_ctrl (
  input  [2:0] in_1,
  input  [4:0] in_2,
  input  in_3,
  input  in_4,
  input  in_5,
  input  in_6,
  input  in_7,
  output [1:0] PCCNTRL,
  output KILL1,
  output KILL2
);

  wire and_1_out, and_2_out, and_3_out, and_4_out, comparator_2_gt, GTE, JALR, NE, priority_encoder_1_gs;

  or or_1 (GTE, in_1[0], in_1[1]);
  Comparator #(.width(5), .mode("unsigned")) comparator_1 (.a(in_2), .b(5'b10110), .eq(JALR));  // open: gt, lt
  not not_1 (NE, in_1[1]);
  Priority_Encoder #(.select(2), .disabled(0)) priority_encoder_1 (
    .in0(1'b1), .in1(in_3), .in2(KILL2), .in3(JALR), .out(PCCNTRL), .gs(priority_encoder_1_gs));  // open: en_out, en_in
  or or_2 (KILL1, in_3, KILL2);
  and and_1 (and_1_out, in_4, in_1[1]);
  and and_2 (and_2_out, in_5, NE);
  and and_3 (and_3_out, in_6, in_1[2]);
  and and_4 (and_4_out, in_7, GTE);
  or or_3 (KILL2, and_1_out, and_2_out, and_3_out, and_4_out);
  Comparator #(.width(5), .mode("unsigned")) comparator_2 (.gt(comparator_2_gt));  // open: a, b, eq, lt

  // Other names for the same wires on the sheet: BEQ = in_4; BGE = in_7; BLT = in_6; BNQ = in_5; BRANCH = KILL2;
  //   GT = in_1[0]; EQ = in_1[1]; LT = in_1[2]; J = in_3; OP[4:0] = in_2
endmodule

module Forward (
  input  [2:0] RD2,
  input  [2:0] RD3,
  input  [2:0] Rd4,
  input  WrWb,
  input  WrMem,
  input  in_6,
  input  WrEx,
  input  [2:0] RS,
  input  [2:0] Rt,
  output [1:0] FrwA,
  output [1:0] FrwB,
  output out_12
);

  wire comparator_1_eq, comparator_2_eq, comparator_6_eq, comparator_7_eq, D0, D1, D2, D3, or_1_out, RS__0,
       RS_Rd2, RS_Rd3, RS_Rd4, RT__0, RT_Rd2, RT_Rd3, RT_Rd4, T0, T1, T2, T3;
  wire [1:0] srcA, srcB;

  Comparator #(.width(3), .mode("unsigned")) comparator_1 (.a(RS), .b(3'b000), .eq(comparator_1_eq));  // open: gt, lt
  Comparator #(.width(2), .mode("unsigned")) comparator_2 (.a(FrwB), .b(2'b01), .eq(comparator_2_eq));  // open: gt, lt
  not not_1 (RS__0, comparator_1_eq);
  Comparator #(.width(3), .mode("unsigned")) comparator_3 (.a(RS), .b(RD2), .eq(RS_Rd2));  // open: gt, lt
  Comparator #(.width(3), .mode("unsigned")) comparator_4 (.a(RS), .b(RD3), .eq(RS_Rd3));  // open: gt, lt
  Comparator #(.width(3), .mode("unsigned")) comparator_5 (.a(RS), .b(Rd4), .eq(RS_Rd4));  // open: gt, lt
  Comparator #(.width(2), .mode("unsigned")) comparator_6 (.a(FrwA), .b(2'b01), .eq(comparator_6_eq));  // open: gt, lt
  or or_1 (or_1_out, comparator_6_eq, comparator_2_eq);
  and and_1 (out_12, in_6, or_1_out);
  and and_2 (D3, RS__0, RS_Rd2, WrEx);
  and and_3 (D2, RS__0, RS_Rd3, WrMem);
  and and_4 (D1, RS__0, RS_Rd4, WrWb);
  nand nand_1 (D0, D1, D3, D2);
  Pencoder pencoder_1 (.in_1(D0), .in_2(D1), .in_3(D2), .in_4(D3), .out_5(srcA[1]), .out_6(srcA[0]));  // open: out_7
  Comparator #(.width(3), .mode("unsigned")) comparator_7 (.a(Rt), .b(3'b000), .eq(comparator_7_eq));  // open: gt, lt
  not not_2 (RT__0, comparator_7_eq);
  Comparator #(.width(3), .mode("unsigned")) comparator_8 (.a(Rt), .b(RD2), .eq(RT_Rd2));  // open: gt, lt
  Comparator #(.width(3), .mode("unsigned")) comparator_9 (.a(Rt), .b(RD3), .eq(RT_Rd3));  // open: gt, lt
  Comparator #(.width(3), .mode("unsigned")) comparator_10 (.a(Rt), .b(Rd4), .eq(RT_Rd4));  // open: gt, lt
  Multiplexer #(.select(2), .width(2), .enable("false")) multiplexer_1 (
    .in0(2'b00), .in1(2'b11), .in2(2'b10), .in3(2'b01), .out(FrwA), .sel(srcA));
  Pencoder pencoder_2 (.in_1(T0), .in_2(T1), .in_3(T2), .in_4(T3), .out_5(srcB[1]), .out_6(srcB[0]));  // open: out_7
  and and_5 (T3, RT__0, RT_Rd2, WrEx);
  and and_6 (T2, RT__0, RT_Rd3, WrMem);
  and and_7 (T1, RT__0, RT_Rd4, WrWb);
  nand nand_2 (T0, T1, T3, T2);
  Multiplexer #(.select(2), .width(2), .enable("false")) multiplexer_2 (
    .in0(2'b00), .in1(2'b11), .in2(2'b10), .in3(2'b01), .out(FrwB), .sel(srcB));

  // Other names for the same wires on the sheet: MemRd = in_6
endmodule

module Pencoder (
  input  in_1,
  input  in_2,
  input  in_3,
  input  in_4,
  output out_5,
  output out_6,
  output out_7
);

  wire and_1_out, not_1_out;

  not not_1 (not_1_out, in_3);
  and and_1 (and_1_out, not_1_out, in_2);
  or or_1 (out_5, in_3, in_4);
  or or_2 (out_6, in_4, and_1_out);
  or or_3 (out_7, in_1, in_2, in_3, in_4);

  // Other names for the same wires on the sheet: d0 = in_1; d1 = in_2; d2 = in_3; d3 = in_4
endmodule
